// Logisim project hw2.circ as structural Verilog: 1 circuit, main circuit main
module main (
  input  x,
  input  y,
  input  z,
  input  in_4,
  input  in_5,
  input  in_6,
  input  in_7,
  input  in_8,
  input  in_9,
  input  in_10,
  input  in_11,
  input  in_12,
  output f,
  output out_14,
  output out_15,
  output out_16
);

  wire and_1_out, and_2_out, and_3_out, and_4_out, nand_1_out, nand_2_out, nand_3_out, nand_4_out,
       nand_5_out, not_1_out, not_2_out, not_3_out, not_4_out, not_5_out, not_6_out, not_7_out;

  not not_1 (not_1_out, y);
  not not_2 (not_2_out, in_5);
  not not_3 (not_3_out, in_8);
  and and_1 (and_1_out, x, not_1_out);
  and and_2 (and_2_out, y, z);
  and and_3 (and_3_out, in_4, not_2_out);
  and and_4 (and_4_out, in_5, in_6);
  not not_4 (not_4_out, and_3_out);
  nand nand_1 (nand_1_out, in_7, not_3_out);
  nand nand_2 (nand_2_out, in_8, in_9);
  nand nand_3 (nand_3_out, in_11, in_11);
  or or_1 (f, and_1_out, and_2_out);
  not not_5 (not_5_out, not_4_out);
  not not_6 (not_6_out, nand_1_out);
  not not_7 (not_7_out, nand_2_out);
  nand nand_4 (nand_4_out, in_10, nand_3_out);
  nand nand_5 (nand_5_out, in_11, in_12);
  or or_2 (out_14, not_5_out, and_4_out);
  or or_3 (out_15, not_6_out, not_7_out);
  nand nand_6 (out_16, nand_4_out, nand_5_out);
endmodule
